// Digital circuit ALU.dig as structural Verilog
module ALU (
  input  [31:0] a,
  input  [31:0] b,
  input  [2:0] op,
  output [31:0] res,
  output isZero,
  output [31:0] high,
  output [31:0] lo
);

  wire comparator_2_eq, comparator_3_eq, div1, div2;
  wire [0:0] comparator_1_lt;
  wire [31:0] add_1_s, and_1_out, ml1, mul2, or_1_out, sub_1_s, xor_1_out;

  assign and_1_out = a & b;  // And and_1, 32 bits wide
  assign or_1_out = a | b;  // Or or_1, 32 bits wide
  Add #(.Bits(32)) add_1 (.a(a), .b(b), .c_i(1'b0), .s(add_1_s));  // open: c_o
  Sub #(.Bits(32)) sub_1 (.a(a), .b(b), .c_i(1'b0), .s(sub_1_s));  // open: c_o
  Comparator #(.Signed("true"), .Bits(32)) comparator_1 (.a(a), .b(b), .lt(comparator_1_lt[0]));  // open: gt, eq
  assign xor_1_out = a ^ b;  // XOr xor_1, 32 bits wide
  Mul #(.Signed("true"), .Bits(32)) mul_1 (.a(a), .b(b), .mul({mul2, ml1}));
  div div_1 (.divisor(a), .dividend(b));  // open: quotient, remainder
  Multiplexer #(.Selector_Bits(3), .Bits(32)) multiplexer_1 (
    .sel(op), .in_0(and_1_out), .in_1(or_1_out), .in_2(add_1_s), .in_3(sub_1_s),
    .in_4({{31{1'b0}}, comparator_1_lt[0]}), .in_5(xor_1_out), .in_6({32{1'b0}}), .in_7({32{1'b0}}), .out(res));
  Comparator comparator_2 (.a(op[0]), .b(1'b1), .eq(comparator_2_eq));  // open: gt, lt
  Comparator comparator_3 (.a(op[0]), .b(1'b1), .eq(comparator_3_eq));  // open: gt, lt
  Comparator #(.Bits(32)) comparator_4 (.a(res), .b({32{1'b0}}), .eq(isZero));  // open: gt, lt
  Multiplexer multiplexer_2 (.sel(comparator_2_eq), .in_0(div1), .in_1(ml1[0]), .out(lo[0]));
  Multiplexer multiplexer_3 (.sel(comparator_3_eq), .in_0(div2), .in_1(mul2[0]), .out(high[0]));
  // Pins of 1 and 3 bits meet at op
  // Pins of 1 and 32 bits meet at high
  // Pins of 1 and 32 bits meet at ml1
  // Pins of 1 and 32 bits meet at mul2
  // Pins of 1 and 32 bits meet at lo
  // Pins of 1 and 3 bits meet at 3'b111
  // Pins of 1 and 3 bits meet at 3'b111

  // Other names for the same wires on the sheet: mux[2:0] = op
endmodule
