// Digital circuit ALUControl.dig as structural Verilog
module ALUControl (
  input  [2:0] aluOp,
  input  [5:0] Func,
  output [2:0] aluFunc
);

  wire ADD_eq, AND_eq, comparator_1_eq, div_eq, mult_eq, OR_eq, priorityencoder_1_any, SLT_eq, SUB_eq, xor_eq;
  wire [2:0] multiplexer_1_out, priorityencoder_1_num;

  Comparator #(.Bits(6)) AND (.a(Func), .b(6'b100100), .eq(AND_eq));  // open: gt, lt
  Comparator #(.Bits(6)) OR (.a(Func), .b(6'b100101), .eq(OR_eq));  // open: gt, lt
  Comparator #(.Bits(6)) ADD (.a(Func), .b(6'b100000), .eq(ADD_eq));  // open: gt, lt
  Comparator #(.Bits(6)) SUB (.a(Func), .b(6'b100010), .eq(SUB_eq));  // open: gt, lt
  Comparator #(.Bits(6)) SLT (.a(Func), .b(6'b101010), .eq(SLT_eq));  // open: gt, lt
  Comparator #(.Bits(6)) \xor  (.a(Func), .b(6'b100110), .eq(xor_eq));  // open: gt, lt
  Comparator #(.Bits(6)) mult (.a(Func), .b(6'b011000), .eq(mult_eq));  // open: gt, lt
  Comparator #(.Bits(6)) div (.a(Func), .b(6'b011010), .eq(div_eq));  // open: gt, lt
  PriorityEncoder #(.Selector_Bits(3)) priorityencoder_1 (
    .in0(AND_eq), .in1(OR_eq), .in2(ADD_eq), .in3(SUB_eq), .in4(SLT_eq), .in5(xor_eq), .in6(mult_eq),
    .in7(div_eq), .num(priorityencoder_1_num), .any(priorityencoder_1_any));
  Multiplexer #(.Bits(3)) multiplexer_1 (
    .sel(priorityencoder_1_any), .in_0(3'b110), .in_1(priorityencoder_1_num), .out(multiplexer_1_out));
  Comparator #(.Bits(3)) comparator_1 (.a(aluOp), .b(3'b111), .eq(comparator_1_eq));  // open: gt, lt
  Multiplexer #(.Bits(3)) multiplexer_2 (.sel(comparator_1_eq), .in_0(aluOp), .in_1(multiplexer_1_out), .out(aluFunc));

  // Other names for the same wires on the sheet: f[5:0] = Func; op[2:0] = aluOp
endmodule
