// Digital circuit ControlUnit.dig as structural Verilog
module ControlUnit (
  input  [5:0] Opcode,
  input  Reset,
  output aluSrc,
  output RegDst,
  output [2:0] aluOp,
  output memToReg,
  output memRead,
  output memWrite,
  output RegWrite,
  output branch,
  output jump,
  output branch2,
  output lup
);

  wire addi_eq, andi_eq, Beq_eq, Bne_eq, jump_eq, lui_eq, LW_eq, ori_eq, rformat_eq, SW_eq, xori_eq;
  wire [3:0] priorityencoder_1_num;
  wire [12:0] multiplexer_1_out;

  Comparator #(.Bits(6)) rformat (.a(Opcode), .b({6{1'b0}}), .eq(rformat_eq));  // open: gt, lt
  Comparator #(.Bits(6)) SW (.a(Opcode), .b(6'b101011), .eq(SW_eq));  // open: gt, lt
  Comparator #(.Bits(6)) LW (.a(Opcode), .b(6'b100011), .eq(LW_eq));  // open: gt, lt
  Comparator #(.Bits(6)) Beq (.a(Opcode), .b(6'b000100), .eq(Beq_eq));  // open: gt, lt
  Comparator #(.Bits(6)) Bne (.a(Opcode), .b(6'b000101), .eq(Bne_eq));  // open: gt, lt
  Comparator #(.Bits(6)) u_jump (.a(Opcode), .b(6'b000010), .eq(jump_eq));  // open: gt, lt
  Comparator #(.Bits(6)) addi (.a(Opcode), .b(6'b001000), .eq(addi_eq));  // open: gt, lt
  Comparator #(.Bits(6)) andi (.a(Opcode), .b(6'b001100), .eq(andi_eq));  // open: gt, lt
  Comparator #(.Bits(6)) ori (.a(Opcode), .b(6'b001101), .eq(ori_eq));  // open: gt, lt
  Comparator #(.Bits(6)) xori (.a(Opcode), .b(6'b001110), .eq(xori_eq));  // open: gt, lt
  Comparator #(.Bits(6)) lui (.a(Opcode), .b(6'b001111), .eq(lui_eq));  // open: gt, lt
  PriorityEncoder #(.Selector_Bits(4)) priorityencoder_1 (
    .in0(rformat_eq), .in1(SW_eq), .in2(LW_eq), .in3(Beq_eq), .in4(Bne_eq), .in5(jump_eq), .in6(addi_eq),
    .in7(andi_eq), .in8(ori_eq), .in9(xori_eq), .in10(lui_eq), .in11(1'b0), .in12(1'b0), .in13(1'b0),
    .in14(1'b0), .in15(1'b0), .num(priorityencoder_1_num));  // open: any
  Multiplexer #(.Selector_Bits(4), .Bits(13)) multiplexer_1 (
    .sel(priorityencoder_1_num), .in_0(13'h178), .in_1(13'h91), .in_2(13'h196), .in_3(13'h218),
    .in_4(13'h818), .in_5(13'h400), .in_6(13'h190), .in_7(13'h180), .in_8(13'h188), .in_9(13'h1a8),
    .in_10(13'h11a8), .in_11({13{1'b0}}), .in_12({13{1'b0}}), .in_13({13{1'b0}}), .in_14({13{1'b0}}),
    .in_15({13{1'b0}}), .out(multiplexer_1_out));
  Multiplexer #(.Bits(13)) multiplexer_2 (
    .sel(Reset), .in_0(multiplexer_1_out), .in_1({13{1'b0}}),
    .out({lup, branch2, jump, branch, RegWrite, aluSrc, RegDst, aluOp, memToReg, memRead, memWrite}));

  // Other names for the same wires on the sheet: opc[5:0] = Opcode; rst = Reset

  // Notes on the sheet:
  //   Reset: RESET input
endmodule
