// Digital circuit DataMemory.dig as structural Verilog
module DataMemory (
  input  [31:0] virtualPC,
  input  en,
  output invalidMemory,
  output [10:0] Physicaladdress
);

  wire adder, comparator_1_lt, comparator_2_gt, comparator_3_lt, comparator_4_gt, control, or_2_out;
  wire [31:0] add_1_s, multiplexer_1_out, multiplexer_2_out;
  wire [31:11] multiplexer_3_out;

  Comparator #(.Bits(32)) comparator_1 (.a(virtualPC), .b(32'h7fffebfc), .lt(comparator_1_lt));  // open: gt, eq
  Comparator #(.Bits(32)) comparator_2 (.a(virtualPC), .b(32'h7fffeffb), .gt(comparator_2_gt));  // open: eq, lt
  Comparator #(.Bits(32)) comparator_3 (.a(virtualPC), .b(32'h10000000), .lt(comparator_3_lt));  // open: gt, eq
  Comparator #(.Bits(32)) comparator_4 (.a(virtualPC), .b(32'h100003ff), .gt(comparator_4_gt));  // open: eq, lt
  or or_1 (adder, comparator_1_lt, comparator_2_gt);
  or or_2 (or_2_out, comparator_3_lt, comparator_4_gt);
  Multiplexer #(.Bits(32)) multiplexer_1 (.sel(control), .in_0(virtualPC), .in_1({32{1'b0}}), .out(multiplexer_1_out));
  and and_1 (control, adder, or_2_out);
  Multiplexer #(.Bits(32)) multiplexer_2 (
    .sel(en), .in_0({32{1'b0}}), .in_1(multiplexer_1_out), .out(multiplexer_2_out));
  Add #(.Bits(32)) add_1 (.a(multiplexer_2_out), .b(32'h4), .c_i(1'b0), .s(add_1_s));  // open: c_o
  Multiplexer #(.Bits(32)) multiplexer_3 (
    .sel(adder), .in_0(add_1_s), .in_1(multiplexer_2_out), .out({multiplexer_3_out, Physicaladdress}));
  Multiplexer multiplexer_4 (.sel(en), .in_0(1'b0), .in_1(control), .out(invalidMemory));
endmodule

/* Test case:
virtualPC    Physicaladdress  invalidMemory
repeat (4)  (0x400000+n) (n)          0
            0x4003FF      X           0
            0x400400      X           1
            0x3FFFFC      X           1
            0x4003FD     0x3FD        0
*/
