// Digital circuit MIPS32SOC.dig as structural Verilog
module MIPS32SOC (
  input  clk,
  input  rst,
  output invalid_opcode,
  output invalid_addr,
  output invalid_pc
);

  wire aluSrc, and_1_out, and_2_out, branch, branch2, ctrl, isZero, jorbr, jump, lup, memRead, memToReg,
       memWrite, mxd, not_1_out, readorwrite, RegDst, RegWrite;
  wire [2:0] aluFunc, aluOp;
  wire [4:0] multiplexer_3_out, Ra, Rb;
  wire [5:0] Func, Opcode;
  wire [9:0] dirvirtual_1_physicaladdress;
  wire [10:0] datamemory_1_physicaladdress;
  wire [31:0] alu_1_high, alu_1_lo, alu_1_res, beqoffset, bitextender_1_out, Data_Mem_d, jumpoffset, l, ll,
       multiplexer_1_out, multiplexer_2_out, multiplexer_4_out, multiplexer_5_out, multiplexer_6_out,
       multiplexer_8_out, offset, offsetgeneral, PC_q, pcplus4, Reg_File_da, Reg_File_db;
  wire [31:22] reslui;

  Multiplexer #(.Bits(32)) multiplexer_1 (
    .sel(jorbr), .in_0(multiplexer_2_out), .in_1(offsetgeneral), .out(multiplexer_1_out));
  Multiplexer #(.Bits(32)) multiplexer_2 (.sel(rst), .in_0(pcplus4), .in_1(32'h400000), .out(multiplexer_2_out));
  Register #(.Bits(32)) PC (.D(multiplexer_1_out), .C(clk), .en(1'b1), .Q(PC_q));
  DirVirtual dirvirtual_1 (
    .virtualPC(PC_q), .invalidMemory(invalid_pc), .Physicaladdress(dirvirtual_1_physicaladdress));
  ControlUnit controlunit_1 (
    .Opcode(Opcode), .Reset(rst), .aluSrc(aluSrc), .RegDst(RegDst), .aluOp(aluOp), .memToReg(memToReg),
    .memRead(memRead), .memWrite(memWrite), .RegWrite(RegWrite), .branch(branch), .jump(jump),
    .branch2(branch2), .lup(lup));
  Add #(.Bits(32)) add_1 (.a(PC_q), .b(32'h4), .c_i(1'b0), .s(pcplus4));  // open: c_o
  ALUControl alucontrol_1 (.aluOp(aluOp), .Func(Func), .aluFunc(aluFunc));
  ROM #(.AddrBits(8), .Bits(32)) InstMem (
    .A(dirvirtual_1_physicaladdress[9:2]), .sel(1'b1), .D({Opcode, Ra, Rb, reslui, Func}));
  muxadd muxadd_1 (.in(Opcode), .out(mxd));
  jtarget jtarget_1 (.jumpadress({Ra, Rb, reslui, Func}), .pc_plus_4(pcplus4), .out(jumpoffset));
  Multiplexer #(.Bits(5)) multiplexer_3 (.sel(RegDst), .in_0(Rb), .in_1(reslui[31:27]), .out(multiplexer_3_out));
  BitExtender #(.inputBits(16), .outputBits(32)) bitextender_1 (.in({reslui, Func}), .out(bitextender_1_out));
  RegisterFile #(.AddrBits(5), .Bits(32)) Reg_File (
    .Din(multiplexer_8_out), .we(RegWrite), .Rw(multiplexer_3_out), .C(clk), .Ra(Ra), .Rb(Rb),
    .Da(Reg_File_da), .Db(Reg_File_db));
  ShiftLeft2 shiftleft2_1 (.i(bitextender_1_out), .o(offset));
  Multiplexer #(.Bits(32)) multiplexer_4 (
    .sel(mxd), .in_0(bitextender_1_out), .in_1({{16{1'b0}}, reslui, Func}), .out(multiplexer_4_out));
  Multiplexer #(.Bits(32)) multiplexer_5 (
    .sel(lup), .in_0(multiplexer_4_out), .in_1({reslui, Func, {16{1'b0}}}), .out(multiplexer_5_out));
  Multiplexer #(.Bits(32)) multiplexer_6 (
    .sel(aluSrc), .in_0(Reg_File_db), .in_1(multiplexer_5_out), .out(multiplexer_6_out));
  ALU alu_1 (
    .a(Reg_File_da), .b(multiplexer_6_out), .op(aluFunc), .res(alu_1_res), .isZero(isZero),
    .high(alu_1_high), .lo(alu_1_lo));
  not not_1 (not_1_out, isZero);
  Register #(.Bits(32)) High (.D(alu_1_high), .C(clk), .en(1'b1), .Q(ll));
  Register #(.Bits(32)) Low (.D(alu_1_lo), .C(clk), .en(1'b1), .Q(l));
  Add #(.Bits(32)) add_2 (.a(pcplus4), .b(offset), .c_i(1'b0), .s(beqoffset));  // open: c_o
  and and_1 (and_1_out, branch, isZero);
  and and_2 (and_2_out, branch2, not_1_out);
  DataMemory datamemory_1 (
    .virtualPC(alu_1_res), .en(readorwrite), .invalidMemory(invalid_addr),
    .Physicaladdress(datamemory_1_physicaladdress));
  or or_1 (ctrl, and_1_out, and_2_out);
  Multiplexer #(.Bits(32)) multiplexer_7 (.sel(jump), .in_0(beqoffset), .in_1(jumpoffset), .out(offsetgeneral));
  or or_2 (jorbr, jump, ctrl);
  RAMDualPort #(.AddrBits(8), .Bits(32)) Data_Mem (
    .A(datamemory_1_physicaladdress[9:2]), .Din(Reg_File_db), .str(memWrite), .C(clk), .ld(memRead),
    .D(Data_Mem_d));
  Multiplexer #(.Bits(32)) multiplexer_8 (.sel(memToReg), .in_0(alu_1_res), .in_1(Data_Mem_d), .out(multiplexer_8_out));
  or or_3 (readorwrite, memRead, memWrite);

  assign invalid_opcode = 1'b0;

  // Other names for the same wires on the sheet: reslui[21:16] = Func; sll16[15:0] = {reslui, Func};
  //   inv = invalid_addr; invalidmem = invalid_pc

  // Notes on the sheet:
  //   contents of InstMem (hex, n*v repeats v):
  //   308af0f0,8000001,ac080008,0,0,0,0,0,8000001
endmodule
