// Digital circuit StackVir.dig as structural Verilog
module StackVir (
  input  [31:0] virtualPC,
  output invalidMemory,
  output [10:0] Physicaladdress
);

  wire comparator_1_lt, comparator_2_gt;
  wire [31:11] multiplexer_1_out;

  Comparator #(.Bits(32)) comparator_1 (.a(virtualPC), .b(32'h7fffebfc), .lt(comparator_1_lt));  // open: gt, eq
  Comparator #(.Bits(32)) comparator_2 (.a(virtualPC), .b(32'h7fffeffb), .gt(comparator_2_gt));  // open: eq, lt
  or or_1 (invalidMemory, comparator_1_lt, comparator_2_gt);
  Multiplexer #(.Bits(32)) multiplexer_1 (
    .sel(invalidMemory), .in_0(virtualPC), .in_1({32{1'b0}}), .out({multiplexer_1_out, Physicaladdress}));

  // Other names for the same wires on the sheet: control = invalidMemory
endmodule

/* Test case:
virtualPC    Physicaladdress  invalidMemory
repeat (4)  (0x400000+n) (n)          0
            0x4003FF      X           0
            0x400400      X           1
            0x3FFFFC      X           1
            0x4003FD     0x3FD        0
*/
