// Digital circuit dicisor.dig as structural Verilog
module dicisor (
  input  [31:0] divisor,
  input  [31:0] dividend,
  output [31:0] quotient,
  output [31:0] remainder
);

  wire xor_1_out;
  wire [31:0] A1, add_1_s, add_2_s, add_3_s, add_4_s, d, m, montopijagerardo_1_p4, montopijagerardo_1_p5,
       montopijagerardo_2_a1, montopijagerardo_2_q1, montopijagerardo_3_a1, montopijagerardo_3_q1,
       montopijagerardo_4_a1, montopijagerardo_4_q1, montopijagerardo_5_a1, montopijagerardo_5_q1,
       montopijagerardo_6_a1, montopijagerardo_6_q1, montopijagerardo_7_a1, montopijagerardo_7_q1,
       montopijagerardo_8_a1, montopijagerardo_8_q1, montopijagerardo_9_a1, montopijagerardo_9_q1,
       montopijagerardo_10_a1, montopijagerardo_10_q1, montopijagerardo_11_a1, montopijagerardo_11_q1,
       montopijagerardo_12_a1, montopijagerardo_12_q1, montopijagerardo_13_a1, montopijagerardo_13_q1,
       montopijagerardo_14_a1, montopijagerardo_14_q1, montopijagerardo_15_a1, montopijagerardo_15_q1,
       montopijagerardo_16_a1, montopijagerardo_16_q1, montopijagerardo_17_a1, montopijagerardo_17_q1,
       montopijagerardo_18_a1, montopijagerardo_18_q1, montopijagerardo_19_a1, montopijagerardo_19_q1,
       montopijagerardo_20_a1, montopijagerardo_20_q1, montopijagerardo_21_a1, montopijagerardo_21_q1,
       montopijagerardo_22_a1, montopijagerardo_22_q1, montopijagerardo_23_a1, montopijagerardo_23_q1,
       montopijagerardo_24_a1, montopijagerardo_24_q1, montopijagerardo_25_a1, montopijagerardo_25_q1,
       montopijagerardo_26_a1, montopijagerardo_26_q1, montopijagerardo_27_a1, montopijagerardo_27_q1,
       montopijagerardo_28_a1, montopijagerardo_28_q1, montopijagerardo_29_a1, montopijagerardo_29_q1,
       montopijagerardo_30_a1, montopijagerardo_30_q1, montopijagerardo_31_a1, montopijagerardo_31_q1,
       not_1_out, not_2_out, not_3_out, not_4_out, Q1;
  wire [31:4] undriven;

  assign not_1_out[3:0] = ~dividend[3:0];  // Not not_1, 4 bits wide
  // montopijagerardo montopijagerardo_1: pin names not known; wires that end beside it: m, d, 4'b0000, montopijagerardo_1_p4, montopijagerardo_1_p5
  assign not_2_out[3:0] = ~{divisor[31], divisor[2:0]};  // Not not_2, 4 bits wide
  Add #(.Bits(32)) add_1 (.a(not_1_out), .b({32{1'b0}}), .c_i(1'b1), .s(add_1_s));  // open: c_o
  montopijagerardo montopijagerardo_2 (
    .M(m), .Q(montopijagerardo_1_p4), .A(montopijagerardo_1_p5), .Q1(montopijagerardo_2_q1),
    .A1(montopijagerardo_2_a1));
  Add #(.Bits(32)) add_2 (.a(not_2_out), .b({32{1'b0}}), .c_i(1'b1), .s(add_2_s));  // open: c_o
  montopijagerardo montopijagerardo_3 (
    .M(m), .Q(montopijagerardo_2_q1), .A(montopijagerardo_2_a1), .Q1(montopijagerardo_3_q1),
    .A1(montopijagerardo_3_a1));
  Multiplexer #(.Bits(32)) multiplexer_1 (
    .sel(divisor[31]), .in_0({undriven, divisor[31], divisor[2:0]}), .in_1(add_2_s), .out(m));
  Multiplexer #(.Bits(32)) multiplexer_2 (.sel(dividend[31]), .in_0(dividend), .in_1(add_1_s), .out(d));
  montopijagerardo montopijagerardo_4 (
    .M(m), .Q(montopijagerardo_3_q1), .A(montopijagerardo_3_a1), .Q1(montopijagerardo_4_q1),
    .A1(montopijagerardo_4_a1));
  montopijagerardo montopijagerardo_5 (
    .M(m), .Q(montopijagerardo_4_q1), .A(montopijagerardo_4_a1), .Q1(montopijagerardo_5_q1),
    .A1(montopijagerardo_5_a1));
  montopijagerardo montopijagerardo_6 (
    .M(m), .Q(montopijagerardo_5_q1), .A(montopijagerardo_5_a1), .Q1(montopijagerardo_6_q1),
    .A1(montopijagerardo_6_a1));
  montopijagerardo montopijagerardo_7 (
    .M(m), .Q(montopijagerardo_6_q1), .A(montopijagerardo_6_a1), .Q1(montopijagerardo_7_q1),
    .A1(montopijagerardo_7_a1));
  montopijagerardo montopijagerardo_8 (
    .M(m), .Q(montopijagerardo_7_q1), .A(montopijagerardo_7_a1), .Q1(montopijagerardo_8_q1),
    .A1(montopijagerardo_8_a1));
  montopijagerardo montopijagerardo_9 (
    .M(m), .Q(montopijagerardo_8_q1), .A(montopijagerardo_8_a1), .Q1(montopijagerardo_9_q1),
    .A1(montopijagerardo_9_a1));
  montopijagerardo montopijagerardo_10 (
    .M(m), .Q(montopijagerardo_9_q1), .A(montopijagerardo_9_a1), .Q1(montopijagerardo_10_q1),
    .A1(montopijagerardo_10_a1));
  assign not_3_out[3:0] = ~Q1[3:0];  // Not not_3, 4 bits wide
  assign not_4_out[3:0] = ~A1[3:0];  // Not not_4, 4 bits wide
  Add #(.Bits(32)) add_3 (.a(not_3_out), .b({32{1'b0}}), .c_i(1'b1), .s(add_3_s));  // open: c_o
  Add #(.Bits(32)) add_4 (.a(not_4_out), .b({32{1'b0}}), .c_i(1'b1), .s(add_4_s));  // open: c_o
  montopijagerardo montopijagerardo_11 (
    .M(m), .Q(montopijagerardo_10_q1), .A(montopijagerardo_10_a1), .Q1(montopijagerardo_11_q1),
    .A1(montopijagerardo_11_a1));
  xor xor_1 (xor_1_out, divisor[31], dividend[31]);
  montopijagerardo montopijagerardo_12 (
    .M(m), .Q(montopijagerardo_11_q1), .A(montopijagerardo_11_a1), .Q1(montopijagerardo_12_q1),
    .A1(montopijagerardo_12_a1));
  Multiplexer #(.Bits(32)) multiplexer_3 (.sel(xor_1_out), .in_0(Q1), .in_1(add_3_s), .out(quotient));
  Multiplexer #(.Bits(32)) multiplexer_4 (.sel(dividend[31]), .in_0(A1), .in_1(add_4_s), .out(remainder));
  montopijagerardo montopijagerardo_13 (
    .M(m), .Q(montopijagerardo_12_q1), .A(montopijagerardo_12_a1), .Q1(montopijagerardo_13_q1),
    .A1(montopijagerardo_13_a1));
  montopijagerardo montopijagerardo_14 (
    .M(m), .Q(montopijagerardo_13_q1), .A(montopijagerardo_13_a1), .Q1(montopijagerardo_14_q1),
    .A1(montopijagerardo_14_a1));
  montopijagerardo montopijagerardo_15 (
    .M(m), .Q(montopijagerardo_14_q1), .A(montopijagerardo_14_a1), .Q1(montopijagerardo_15_q1),
    .A1(montopijagerardo_15_a1));
  montopijagerardo montopijagerardo_16 (
    .M(m), .Q(montopijagerardo_15_q1), .A(montopijagerardo_15_a1), .Q1(montopijagerardo_16_q1),
    .A1(montopijagerardo_16_a1));
  montopijagerardo montopijagerardo_17 (
    .M(m), .Q(montopijagerardo_16_q1), .A(montopijagerardo_16_a1), .Q1(montopijagerardo_17_q1),
    .A1(montopijagerardo_17_a1));
  montopijagerardo montopijagerardo_18 (
    .M(m), .Q(montopijagerardo_17_q1), .A(montopijagerardo_17_a1), .Q1(montopijagerardo_18_q1),
    .A1(montopijagerardo_18_a1));
  montopijagerardo montopijagerardo_19 (
    .M(m), .Q(montopijagerardo_18_q1), .A(montopijagerardo_18_a1), .Q1(montopijagerardo_19_q1),
    .A1(montopijagerardo_19_a1));
  montopijagerardo montopijagerardo_20 (
    .M(m), .Q(montopijagerardo_19_q1), .A(montopijagerardo_19_a1), .Q1(montopijagerardo_20_q1),
    .A1(montopijagerardo_20_a1));
  montopijagerardo montopijagerardo_21 (
    .M(m), .Q(montopijagerardo_20_q1), .A(montopijagerardo_20_a1), .Q1(montopijagerardo_21_q1),
    .A1(montopijagerardo_21_a1));
  montopijagerardo montopijagerardo_22 (
    .M(m), .Q(montopijagerardo_21_q1), .A(montopijagerardo_21_a1), .Q1(montopijagerardo_22_q1),
    .A1(montopijagerardo_22_a1));
  montopijagerardo montopijagerardo_23 (
    .M(m), .Q(montopijagerardo_22_q1), .A(montopijagerardo_22_a1), .Q1(montopijagerardo_23_q1),
    .A1(montopijagerardo_23_a1));
  montopijagerardo montopijagerardo_24 (
    .M(m), .Q(montopijagerardo_23_q1), .A(montopijagerardo_23_a1), .Q1(montopijagerardo_24_q1),
    .A1(montopijagerardo_24_a1));
  montopijagerardo montopijagerardo_25 (
    .M(m), .Q(montopijagerardo_24_q1), .A(montopijagerardo_24_a1), .Q1(montopijagerardo_25_q1),
    .A1(montopijagerardo_25_a1));
  montopijagerardo montopijagerardo_26 (
    .M(m), .Q(montopijagerardo_25_q1), .A(montopijagerardo_25_a1), .Q1(montopijagerardo_26_q1),
    .A1(montopijagerardo_26_a1));
  montopijagerardo montopijagerardo_27 (
    .M(m), .Q(montopijagerardo_26_q1), .A(montopijagerardo_26_a1), .Q1(montopijagerardo_27_q1),
    .A1(montopijagerardo_27_a1));
  montopijagerardo montopijagerardo_28 (
    .M(m), .Q(montopijagerardo_27_q1), .A(montopijagerardo_27_a1), .Q1(montopijagerardo_28_q1),
    .A1(montopijagerardo_28_a1));
  montopijagerardo montopijagerardo_29 (
    .M(m), .Q(montopijagerardo_28_q1), .A(montopijagerardo_28_a1), .Q1(montopijagerardo_29_q1),
    .A1(montopijagerardo_29_a1));
  montopijagerardo montopijagerardo_30 (
    .M(m), .Q(montopijagerardo_29_q1), .A(montopijagerardo_29_a1), .Q1(montopijagerardo_30_q1),
    .A1(montopijagerardo_30_a1));
  montopijagerardo montopijagerardo_31 (
    .M(m), .Q(montopijagerardo_30_q1), .A(montopijagerardo_30_a1), .Q1(montopijagerardo_31_q1),
    .A1(montopijagerardo_31_a1));
  montopijagerardo montopijagerardo_32 (
    .M(m), .Q(montopijagerardo_31_q1), .A(montopijagerardo_31_a1), .Q1(Q1), .A1(A1));
  // Pins of 4 and 32 bits meet at quotient
  // Pins of 4 and 32 bits meet at remainder
  // Pins of 3 and 31 bits meet at divisor[30:0]
  // Pins of 4 and 32 bits meet at {undriven, divisor[31], divisor[2:0]}
  // Pins of 4 and 32 bits meet at not_2_out
  // Pins of 4 and 32 bits meet at dividend
  // Pins of 4 and 32 bits meet at not_1_out
  // Pins of 4 and 32 bits meet at Q1
  // Pins of 4 and 32 bits meet at not_3_out
  // Pins of 4 and 32 bits meet at A1
  // Pins of 4 and 32 bits meet at not_4_out

  // Other names for the same wires on the sheet: s1 = dividend[31]; s = divisor[31]
endmodule

/* Test case:
dividend divisor quotient remainder
loop(a, 7)
	loop(b, 7)
let nA = a * -1;
let nB = (b+1) * -1;




(a) (b+1) (a/(b+1)) (a%(b+1))
(a) (nB) (a/nB) (a%nB)
(nA) (b+1) (nA/(b+1)) (nA%(b+1))
(nA) (nB) (nA/nB) (nA%nB) 

	end loop
end loop
*/
