// Digital circuit jtarget.dig as structural Verilog
module jtarget (
  input  [25:0] jumpadress,
  input  [31:0] pc_plus_4,
  output [31:0] out
);


  assign out = {pc_plus_4[31:28], jumpadress, 2'b00};
endmodule
