// Digital circuit montopijagerardo.dig as structural Verilog
module montopijagerardo (
  input  [31:0] M,
  input  [31:0] Q,
  input  [31:0] A,
  output [31:0] Q1,
  output [31:0] A1
);

  wire c;
  wire [31:0] sub_1_s;

  Sub #(.Bits(32)) sub_1 (.a({A[30:0], Q[31]}), .b(M), .c_i(1'b0), .s(sub_1_s), .c_o(c));
  Multiplexer #(.Bits(32)) multiplexer_1 (.sel(c), .in_0(sub_1_s), .in_1({A[30:0], Q[31]}), .out(A1));
  not not_1 (Q1[0], c);

  assign Q1[31:1] = Q[30:0];

  // Other names for the same wires on the sheet: a_t[31:0] = {A[30:0], Q[31]}; aa[31:0] = A; t[62:0] = {A[30:0], Q};
  //   q_t[31:1] = Q[30:0]; qq[31:0] = Q
endmodule
