// Digital circuit muxadd.dig as structural Verilog
module muxadd (
  input  [5:0] in,
  output out
);

  wire comparator_1_eq, comparator_2_eq, comparator_3_eq;

  Comparator #(.Bits(6)) comparator_1 (.a(in), .b(6'b001100), .eq(comparator_1_eq));  // open: gt, lt
  Comparator #(.Bits(6)) comparator_2 (.a(in), .b(6'b001101), .eq(comparator_2_eq));  // open: gt, lt
  Comparator #(.Bits(6)) comparator_3 (.a(in), .b(6'b001110), .eq(comparator_3_eq));  // open: gt, lt
  or or_1 (out, comparator_1_eq, comparator_2_eq, comparator_3_eq);
endmodule
